# Fritzing sketch projeto_cliente_hapy (saved by Fritzing 0.8.5b)
breadboards: 2

parts:
  Componente1 = Arduino Uno (Rev3)
  LCD1 = LCD screen
  LED1 = LED - 5mm [color="Green (555nm)" package="5 mm [THT]"]
  LED3 = LED - 5mm [color="Red (635nm)" package="5 mm [THT]"]
  U1 = SD_CARD_SOCKET [package=sdcard_4uconn]
  Componente2 = Real Time Clock Module - DS1307 RTC Breakout Board
  S2 = Round Pushbutton
  S3 = Round Pushbutton  # not connected
  S4 = Round Pushbutton
  R1 = Trimmer Potentiometer [maximum_resistance=10kΩ package=THT]
  LED2 = smd LED [color="Yellow (585nm)" package="0603 [SMD]"]

nets:
  N1: Componente1.A0, LED1.anode, S4.leg0
  N2: Componente1.A1, S2.leg0, LED2.anode
  N3: Componente1.D8, Componente2.SDA
  N4: Componente1.D9_PWM, Componente2.SCL
  N5: Componente1.D10_PWM/SS, Componente2.SQW
  N6: Componente1.D11_PWM/MOSI, LCD1.E
  N7: Componente1.D12/MISO, LCD1.RS
  N8: Componente1.D0/RX, U1.CD_DAT3
  N9: Componente1.D1/TX, U1.SH
  N10: Componente1.D2, LCD1.DB7
  N11: Componente1.D3_PWM, LCD1.DB6
  N12: Componente1.D4, LCD1.DB5
  N13: Componente1.D5_PWM, LCD1.DB4
  5V: Componente1.5V, LCD1.VDD, U1.VDD, Componente2.5V, R1.leg2
  GND: Componente1.GND, LCD1.VSS, LCD1.R/W, LED1.cathode, LED3.cathode, U1.CLK, Componente2.GND, S2.leg1, S4.leg1, R1.leg1, LED2.cathode
  N14: LCD1.V0, R1.wiper
